# Fritzing sketch reaction (saved by Fritzing 0.9.2b)
circuit board: 8.46667cm x 5.64444cm
breadboards: 1

parts:
  Raspberry_Pi1 = Raspberry Pi 2
  LED1 = RGB LED (com. cathode, rgb) [package="5 mm [THT]"]
  LED2 = LED - 5mm [color="Red (633nm)" package="5 mm [THT]"]
  S1 = Pushbutton [package="[THT]"]
  S2 = Pushbutton [package="[THT]"]
  S3 = Pushbutton [package="[THT]"]
  S4 = Pushbutton [package="[THT]"]
  R6 = Resistor [tolerance=±5% resistance=330 package=THT]
  R7 = Resistor [tolerance=±5% resistance=330 package=THT]
  R8 = Resistor [tolerance=±5% resistance=330 package=THT]

nets:
  N1: Raspberry_Pi1.GPIO13, R6.Pin_1
  N2: Raspberry_Pi1.GPIO19, R7.Pin_1
  N3: Raspberry_Pi1.GPIO21, S4.Pin_1, S4.Pin_2
  N4: Raspberry_Pi1.GND, LED1.common_cathode, LED2.cathode, S2.Pin_3, S2.Pin_4, S3.Pin_3, S3.Pin_4, S4.Pin_3, S4.Pin_4
  N5: Raspberry_Pi1.GPIO12, R8.Pin_1
  N6: Raspberry_Pi1.GPIO25, S1.Pin_1, S1.Pin_2
  N7: Raspberry_Pi1.GPIO24, S2.Pin_1, S2.Pin_2
  N8: Raspberry_Pi1.GPIO23, S3.Pin_1, S3.Pin_2
  N9: LED1.red_anode, R7.Pin_0
  N10: LED1.green_anode, R6.Pin_0
  N11: LED2.anode, R8.Pin_0
  N12: S1.Pin_3, S1.Pin_4

notes:
  Start/Stop buttons
  Reaction buttons
