# Fritzing sketch reaction (saved by Fritzing 0.9.2b)
circuit board: 8.46667cm x 5.64444cm
breadboards: 1

parts:
  Raspberry_Pi1 = Raspberry Pi 2
  LED1 = RGB LED (com. cathode, rgb) [package="5 mm [THT]"]
  LED2 = LED - 5mm [color="Red (633nm)" package="5 mm [THT]"]
  S2 = Pushbutton [package="[THT]"]
  S3 = Pushbutton [package="[THT]"]
  S4 = Pushbutton [package="[THT]"]
  R6 = Resistor [tolerance=±5% resistance=330 package=THT]
  R7 = Resistor [tolerance=±5% resistance=330 package=THT]
  R8 = Resistor [tolerance=±5% resistance=330 package=THT]
  R9 = Resistor [tolerance=±5% resistance=330 package=THT]
  S5 = Pushbutton [package="[THT]"]

nets:
  N1: Raspberry_Pi1.GPIO13, R6.Pin_1
  N2: Raspberry_Pi1.GPIO19, R7.Pin_1
  N3: Raspberry_Pi1.GPIO21, S3.Pin_1, S3.Pin_2
  N4: Raspberry_Pi1.GPIO20, R9.Pin_1
  N5: Raspberry_Pi1.GND, LED1.common_cathode, LED2.cathode, S2.Pin_1, S2.Pin_2, S3.Pin_3, S3.Pin_4, S4.Pin_3, S4.Pin_4, S5.Pin_3, S5.Pin_4
  N6: Raspberry_Pi1.GPIO12, R8.Pin_1
  N7: Raspberry_Pi1.GPIO25, S2.Pin_3, S2.Pin_4
  N8: Raspberry_Pi1.GPIO24, S4.Pin_1, S4.Pin_2
  N9: Raspberry_Pi1.GPIO23, S5.Pin_1, S5.Pin_2
  N10: LED1.red_anode, R7.Pin_0
  N11: LED1.green_anode, R6.Pin_0
  N12: LED1.blue_anode, R9.Pin_0
  N13: LED2.anode, R8.Pin_0

notes:
  Start/Stop buttons
  red/blue/green reaction buttons
  RGB led<module fritzingVersion="0.9.2b.11.19.8d2d5970658f0bed09c661c9ea9a515b5f40f44c">
  <boundingRects>
  <boundingRect rect="245.077 -177.808 116.02 37" name="Breadboard View"/>
  <boundingRect rect="0 0 0 0" name="Schematic View"/>
  <boundingRect rect="0 0 0 0" name="PCB View"/>
  </boundingRects>
  <instances>
  <instance modelIndex="85410747" path=":/resources/parts/core/note.fzp" moduleIdRef="NoteModuleID">
  <title>Note1</title>
  <text>&lt;!DOCTYPE HTML PUBLIC "-//W3C//DTD HTML 4.0//EN" "http://www.w3.org/TR/REC-html40/strict.dtd">
  &lt;html>&lt;head>&lt;meta name="qrichtext" content="1" />&lt;style type="text/css">
  p, li { white-space: pre-wrap; }
  &lt;/style>&lt;/head>&lt;body style=" font-family:'Droid Sans'; font-size:9pt; font-weight:400; font-style:normal;">
  &lt;p style=" margin-top:0px; margin-bottom:0px; margin-left:0px; margin-right:0px; -qt-block-indent:0; text-indent:0px;">Start/Stop buttons&lt;/p>&lt;/body>&lt;/html></text>
  <views>
  <breadboardView layer="breadboardNote">
  <geometry width="116.02" height="37" x="245.077" y="-177.808" z="6.50001"/>
  </breadboardView>
  </views>
  </instance>
  </instances>
  </module>
  Proggress indicator
